// Logisim project Jean-Implementations.circ as structural Verilog
module Register_File (
  input  Clock,
  input  [4:0] Rs,
  input  [4:0] Rt,
  input  [4:0] Rd,
  input  [31:0] Write_Data,
  input  Reg_Write,
  input  Clear,
  output [31:0] Read_Data_1,
  output [31:0] Read_Data_2
);

  wire R0_Wreg, R1_Wreg, R2_Wreg, R3_Wreg, R4_Wreg, R5_Wreg, R6_Wreg, R7_Wreg, R8_Wreg, R9_Wreg, R10_Wreg,
       R11_Wreg, R12_Wreg, R13_Wreg, R14_Wreg, R15_Wreg, R16_Wreg, R17_Wreg, R18_Wreg, R19_Wreg, R20_Wreg,
       R21_Wreg, R22_Wreg, R23_Wreg, R24_Wreg, R25_Wreg, R26_Wreg, R27_Wreg, R28_Wreg, R29_Wreg, R30_Wreg,
       R31_Wreg;
  wire [31:0] R1, R2, R3, R4, R5, R6, R7, R8, R9, R10, R11, R12, R13, R14, R15, R16, R17, R18, R19, R20, R21,
       R22, R23, R24, R25, R26, R27, R28, R29, R30, R31;

  Multiplexer #(.select(5), .width(32)) multiplexer_1 (
    .in0({32{1'b0}}), .in1(R1), .in2(R2), .in3(R3), .in4(R4), .in5(R5), .in6(R6), .in7(R7), .in8(R8),
    .in9(R9), .in10(R10), .in11(R11), .in12(R12), .in13(R13), .in14(R14), .in15(R15), .in16(R16), .in17(R17),
    .in18(R18), .in19(R19), .in20(R20), .in21(R21), .in22(R22), .in23(R23), .in24(R24), .in25(R25),
    .in26(R26), .in27(R27), .in28(R28), .in29(R29), .in30(R30), .in31(R31), .out(Read_Data_1), .sel(Rs));  // open: en
  Multiplexer #(.select(5), .width(32)) multiplexer_2 (
    .in0({32{1'b0}}), .in1(R1), .in2(R2), .in3(R3), .in4(R4), .in5(R5), .in6(R6), .in7(R7), .in8(R8),
    .in9(R9), .in10(R10), .in11(R11), .in12(R12), .in13(R13), .in14(R14), .in15(R15), .in16(R16), .in17(R17),
    .in18(R18), .in19(R19), .in20(R20), .in21(R21), .in22(R22), .in23(R23), .in24(R24), .in25(R25),
    .in26(R26), .in27(R27), .in28(R28), .in29(R29), .in30(R30), .in31(R31), .out(Read_Data_2), .sel(Rt));  // open: en
  Decoder #(.select(5)) decoder_1 (
    .out0(R0_Wreg), .out1(R1_Wreg), .out2(R2_Wreg), .out3(R3_Wreg), .out4(R4_Wreg), .out5(R5_Wreg),
    .out6(R6_Wreg), .out7(R7_Wreg), .out8(R8_Wreg), .out9(R9_Wreg), .out10(R10_Wreg), .out11(R11_Wreg),
    .out12(R12_Wreg), .out13(R13_Wreg), .out14(R14_Wreg), .out15(R15_Wreg), .out16(R16_Wreg),
    .out17(R17_Wreg), .out18(R18_Wreg), .out19(R19_Wreg), .out20(R20_Wreg), .out21(R21_Wreg),
    .out22(R22_Wreg), .out23(R23_Wreg), .out24(R24_Wreg), .out25(R25_Wreg), .out26(R26_Wreg),
    .out27(R27_Wreg), .out28(R28_Wreg), .out29(R29_Wreg), .out30(R30_Wreg), .out31(R31_Wreg), .sel(Rd));  // open: en
  Register #(.width(32)) R (.D(Write_Data), .en(R1_Wreg), .Q(R1), .clk(Clock), .clr(Clear));
  Register #(.width(32)) R_2 (.D(Write_Data), .en(R2_Wreg), .Q(R2), .clk(Clock), .clr(Clear));
  Register #(.width(32)) R_3 (.D(Write_Data), .en(R3_Wreg), .Q(R3), .clk(Clock), .clr(Clear));
  Register #(.width(32)) R_4 (.D(Write_Data), .en(R4_Wreg), .Q(R4), .clk(Clock), .clr(Clear));
  Register #(.width(32)) R_5 (.D(Write_Data), .en(R5_Wreg), .Q(R5), .clk(Clock), .clr(Clear));
  Register #(.width(32)) R_6 (.D(Write_Data), .en(R6_Wreg), .Q(R6), .clk(Clock), .clr(Clear));
  Register #(.width(32)) R_7 (.D(Write_Data), .en(R7_Wreg), .Q(R7), .clk(Clock), .clr(Clear));
  Register #(.width(32)) R_8 (.D(Write_Data), .en(R8_Wreg), .Q(R8), .clk(Clock), .clr(Clear));
  Register #(.width(32)) R_9 (.D(Write_Data), .en(R9_Wreg), .Q(R9), .clk(Clock), .clr(Clear));
  Register #(.width(32)) R_10 (.D(Write_Data), .en(R10_Wreg), .Q(R10), .clk(Clock), .clr(Clear));
  Register #(.width(32)) R_11 (.D(Write_Data), .en(R11_Wreg), .Q(R11), .clk(Clock), .clr(Clear));
  Register #(.width(32)) R_12 (.D(Write_Data), .en(R12_Wreg), .Q(R12), .clk(Clock), .clr(Clear));
  Register #(.width(32)) R_13 (.D(Write_Data), .en(R13_Wreg), .Q(R13), .clk(Clock), .clr(Clear));
  Register #(.width(32)) R_14 (.D(Write_Data), .en(R14_Wreg), .Q(R14), .clk(Clock), .clr(Clear));
  Register #(.width(32)) R_15 (.D(Write_Data), .en(R15_Wreg), .Q(R15), .clk(Clock), .clr(Clear));
  Register #(.width(32)) R_16 (.D(Write_Data), .en(R16_Wreg), .Q(R16), .clk(Clock), .clr(Clear));
  Register #(.width(32)) R_17 (.D(Write_Data), .en(R17_Wreg), .Q(R17), .clk(Clock), .clr(Clear));
  Register #(.width(32)) R_18 (.D(Write_Data), .en(R18_Wreg), .Q(R18), .clk(Clock), .clr(Clear));
  Register #(.width(32)) R_19 (.D(Write_Data), .en(R19_Wreg), .Q(R19), .clk(Clock), .clr(Clear));
  Register #(.width(32)) R_20 (.D(Write_Data), .en(R20_Wreg), .Q(R20), .clk(Clock), .clr(Clear));
  Register #(.width(32)) R_21 (.D(Write_Data), .en(R21_Wreg), .Q(R21), .clk(Clock), .clr(Clear));
  Register #(.width(32)) R_22 (.D(Write_Data), .en(R23_Wreg), .Q(R22), .clk(Clock), .clr(Clear));
  Register #(.width(32)) R_23 (.D(Write_Data), .en(R23_Wreg), .Q(R23), .clk(Clock), .clr(Clear));
  Register #(.width(32)) R_24 (.D(Write_Data), .en(R24_Wreg), .Q(R24), .clk(Clock), .clr(Clear));
  Register #(.width(32)) R_25 (.D(Write_Data), .en(R25_Wreg), .Q(R25), .clk(Clock), .clr(Clear));
  Register #(.width(32)) R_26 (.D(Write_Data), .en(R26_Wreg), .Q(R26), .clk(Clock), .clr(Clear));
  Register #(.width(32)) R_27 (.D(Write_Data), .en(R27_Wreg), .Q(R27), .clk(Clock), .clr(Clear));
  Register #(.width(32)) R_28 (.D(Write_Data), .en(R28_Wreg), .Q(R28), .clk(Clock), .clr(Clear));
  Register #(.width(32)) R_29 (.D(Write_Data), .en(R29_Wreg), .Q(R29), .clk(Clock), .clr(Clear));
  Register #(.width(32)) R_30 (.D(Write_Data), .en(R30_Wreg), .Q(R30), .clk(Clock), .clr(Clear));
  Register #(.width(32)) R_31 (.D(Write_Data), .en(R31_Wreg), .Q(R31), .clk(Clock), .clr(Clear));

  // Other names for the same wires on the sheet: CLK = Clock; WData[31:0] = Write_Data; WReg = Reg_Write

  // Notes on the sheet:
  //   Registers
endmodule
