// Logisim project Ray-Implementations.circ as structural Verilog
module ALU (
  input  [3:0] S,
  input  [31:0] A,
  input  [31:0] B,
  output [31:0] R,
  output [31:0] hi,
  output sign,
  output zero,
  output [31:0] lo
);

  wire comparator_2_lt, comparator_3_lt;
  wire [31:0] ADD, AND, NOR, OR, SLT, SLTU, SUB, XOR;

  // Probe on A
  // Probe on B
  // Probe on R
  Comparator #(.width(32)) comparator_1 (.a(R), .b({32{1'b0}}), .gt(sign), .eq(zero));  // open: lt
  Adder #(.width(32)) adder_1 (.a(A), .b(B), .out(ADD));  // open: cin, cout
  Subtractor #(.width(32)) subtractor_1 (.a(A), .b(B), .out(SUB));  // open: bin, bout
  Multiplier #(.width(32)) multiplier_1 (.a(A), .b(B), .out(lo), .cout(hi));  // open: cin
  Divider #(.width(32)) divider_1 (.a(A), .b(B), .out(lo), .rem(hi));  // open: upper
  DivS DIVS (.A(A), .B(B), .LowOutput(lo), .HighOutput(hi));
  assign OR = A | B;  // OR_Gate or_1, 32 bits wide
  assign AND = A & B;  // AND_Gate and_1, 32 bits wide
  assign NOR = ~(A | B);  // NOR_Gate nor_1, 32 bits wide
  assign XOR = A ^ B;  // XOR_Gate xor_1, 32 bits wide
  Comparator #(.width(32)) comparator_2 (.a(A), .b(B), .lt(comparator_2_lt));  // open: gt, eq
  Comparator #(.width(32), .mode("unsigned")) comparator_3 (.a(A), .b(B), .lt(comparator_3_lt));  // open: gt, eq
  Multiplexer #(.width(32), .enable("false")) multiplexer_1 (
    .in0({32{1'b0}}), .in1(32'h1), .out(SLT), .sel(comparator_2_lt));
  Multiplexer #(.width(32), .enable("false")) multiplexer_2 (
    .in0({32{1'b0}}), .in1(32'h1), .out(SLTU), .sel(comparator_3_lt));
  Multiplexer #(.select(4), .width(32), .enable("false")) multiplexer_3 (
    .in0(ADD), .in1(SUB), .out(R), .sel(S));  // open: in2, in3, in4, in5, in6, in7, in8, in9, in10, in11, in12, in13, in14, in15

  // Other names for the same wires on the sheet: RESULT[31:0] = R; SELECT[3:0] = S

  // Notes on the sheet:
  //   ARITMÉTICA
  //   MULU
  //   DIVU
  //   LÓGICA
  //   COMPARACIÓN
  //   revisar signo
endmodule

module DivS (
  input  [31:0] A,
  input  [31:0] B,
  output [31:0] LowOutput,
  output [31:0] HighOutput
);

  wire xor_1_out;
  wire [31:0] divider_1_out, multiplexer_1_out, multiplexer_2_out, negator_1_out, negator_2_out,
       negator_3_out;

  Negator #(.width(32)) negator_1 (.in(A), .out(negator_1_out));
  Negator #(.width(32)) negator_2 (.in(B), .out(negator_2_out));
  Multiplexer #(.width(32), .enable("false")) multiplexer_1 (
    .in0(A), .in1(negator_1_out), .out(multiplexer_1_out), .sel(A[31]));
  Multiplexer #(.width(32), .enable("false")) multiplexer_2 (
    .in0(B), .in1(negator_2_out), .out(multiplexer_2_out), .sel(B[31]));
  Divider #(.width(32)) divider_1 (
    .a(multiplexer_1_out), .b(multiplexer_2_out), .out(divider_1_out), .rem(HighOutput));  // open: upper
  Negator #(.width(32)) negator_3 (.in(divider_1_out), .out(negator_3_out));
  xor xor_1 (xor_1_out, A[31], B[31]);
  // Probe on LowOutput
  Multiplexer #(.width(32), .enable("false")) multiplexer_3 (
    .in0(divider_1_out), .in1(negator_3_out), .out(LowOutput), .sel(xor_1_out));
  // Probe on HighOutput

  // Notes on the sheet:
  //   SIGNED DIV
endmodule
